# Fritzing sketch proton2 (saved by Fritzing 0.9.2b)
perfboards: 2

parts:
  S1 = Pushbutton [package="[THT]"]
  J1 = female pin header, 12 pins [form="♀ (female)"]
  J4 = female pin header, 12 pins [form="♀ (female)"]
  Part1 = Photon  # not connected
  Part2 = Photon  # not connected
  DHT2 = DHT22 Humidity and Temperature Sensor
  R2 = Resistor [tolerance=±5% resistance=4.7k package=THT]
  R3 = Resistor [tolerance=±5% resistance=2k package=THT]
  R4 = Resistor [tolerance=±5% resistance=47 package=THT]
  J2 = male pin header, 25 pins [form="♂ (male)"]
  J3 = male pin header, 25 pins [form="♂ (male)"]
  S2 = Pushbutton [package="[THT]"]
  J6 = female pin header, 4 pins [form="♀ (female)"]
  J7 = male pin header, 4 pins [form="♂ (male)"]
  J8 = male pin header, 4 pins [form="♂ (male)"]
  J5 = male pin header, 4 pins [form="♂ (male)"]
  J9 = male pin header, 4 pins [form="♂ (male)"]
  R5 = Resistor [tolerance=±5% resistance=47 package=THT]

nets:
  N1: S1.Pin_1, S1.Pin_2, J3.pin23
  N2: S1.Pin_3, S1.Pin_4, J1.pin1, J5.pin3, J5.pin4
  N3: J1.pin11, DHT2.GND
  N4: J4.pin7, DHT2.DATA, R2.Pin_1
  N5: J4.pin12, R2.Pin_0
  N6: R3.Pin_1, J2.pin7
  N7: R4.Pin_1, J3.pin20
  N8: J3.pin22, J5.pin1, J5.pin2
  N9: S2.Pin_1, S2.Pin_2, J9.pin1
  N10: S2.Pin_3, S2.Pin_4, J8.pin3, J8.pin4, R5.Pin_0
  N11: J6.pin4, J8.pin1, J8.pin2, J9.pin4
  N12: J7.pin4, R5.Pin_1
