# Fritzing sketch proton (saved by Fritzing 0.9.2b)
perfboards: 1

parts:
  S1 = Pushbutton [package="[THT]"]
  Part1 = Photon
  DHT1 = DHT22 Humidity and Temperature Sensor
  R1 = Resistor [tolerance=±5% resistance=4.7 package=THT]
  J4 = male pin header, 2 pins [form="♂ (male)"]
  R3 = Resistor [tolerance=±5% resistance=100 package=THT]
  J5 = male pin header, 4 pins [form="♂ (male)"]
  Q3 = NPN-Transistor [package="TO92 [THT]"]
  Q4 = NPN-Transistor [package="TO92 [THT]"]
  R4 = Resistor [tolerance=±5% resistance=47 package=THT]
  LED1 = LED - 5mm [color="Red (633nm)" package="5 mm [THT]"]
  R5 = Resistor [tolerance=±5% resistance=2.2k package=THT]
  J3 = male pin header, 2 pins [form="♂ (male)"]
  J6 = male pin header, 2 pins [form="♂ (male)"]  # not connected

nets:
  N1: S1.Pin_1, S1.Pin_2, Q4.C
  N2: S1.Pin_3, S1.Pin_4, Part1.A0, R3.Pin_1
  N3: Part1.A1, J5.pin3
  N4: Part1.A2, J5.pin2
  N5: Part1.A3, J5.pin1
  N6: Part1.A4, Q3.E
  N7: Part1.A5, R5.Pin_0
  GND: Part1.GND, DHT1.GND, J3.pin2
  N8: Part1.VIN, J3.pin1
  N9: Part1.D6, DHT1.DATA, R1.Pin_1
  N10: Part1.3V3, R1.Pin_0
  N11: J4.pin1, R3.Pin_0
  N12: Q4.E, LED1.anode
  N13: Q4.B, R5.Pin_1
  N14: R4.Pin_1, LED1.cathode
